# Fritzing sketch SandwichBoxBot (saved by Fritzing 0.9.3b)
breadboards: 1

parts:
  U1 = NodeMCU V1.0
  J1 = Infrared Proximity Sensor
  J2 = Infrared Proximity Sensor
  VCC1 = 4 x AAA Battery Mount
  M1 = DC Motor
  M2 = DC Motor
  EDGY_motor_control1 = EDGY
  J3 = Piezo Speaker
  LD1 = LD

nets:
  N1: U1.D0, J1.Vout
  N2: U1.D1, EDGY_motor_control1.A1
  N3: U1.D2, EDGY_motor_control1.B1
  N4: U1.D3, J2.Vout
  VCC: U1.3V3, J1.Vcc, J2.Vcc
  GND: U1.GND, J1.GND, J2.GND, VCC1.-, EDGY_motor_control1.GND, J3.pin1, LD1.cathode
  N5: U1.D5, J3.pin2
  N6: U1.D6, EDGY_motor_control1.A2
  N7: U1.D7, EDGY_motor_control1.B2
  N8: U1.Vin, VCC1.+, EDGY_motor_control1.5V+, LD1.anode
  N9: M1.pin_1, EDGY_motor_control1.A1out
  N10: M1.pin_2, EDGY_motor_control1.B1out
  N11: M2.pin_1, EDGY_motor_control1.A2out
  N12: M2.pin_2, EDGY_motor_control1.B2out

custom parts:
  NodeMCU V1.0: ESP8266 based NodeMCU
  LD: A Generic Red Dot Laser Diode Module (~5mW)
